# Fritzing sketch RoundPCB v2 Sensor Board (saved by Fritzing 0.9.10b)
circuit board: 8.68815cm x 9.44356cm
breadboards: 1

parts:
  U1 = LuaNode32 / ESP32 [part_number=ESP32S-PIN30]
  OLED1 = OLED 128x64 I2C Monochrome Display GND-VDD
  H-BRIDGE = female pin header, 6 pins [form="♀ (female)"]
  ON_---_OFF = SPST Switch [package=switch-spdt_lock.007s]
  1K = Resistor [tolerance=±5% resistance=1k power=0.25 package="1206 [SMD]"]
  1K_2 = Resistor [tolerance=±5% resistance=1k power=0.25 package="1206 [SMD]"]
  2K = Resistor [tolerance=±5% resistance=2.2 power=0.25 package="1206 [SMD]"]
  10K = Resistor [tolerance=±5% resistance=10k power=0.25 package="1206 [SMD]"]
  GSR = Screw terminal - 2 pins [package=THT]
  2K_2 = Resistor [tolerance=±5% resistance=2.2 power=0.25 package="1206 [SMD]"]
  PELTIER = female pin header, 4 pins [form="♀ (female)"]  # not connected
  ECG(39) = female pin header, 3 pins [form="♀ (female)"]
  EOG(34) = female pin header, 3 pins [form="♀ (female)"]
  EEG(32) = female pin header, 3 pins [form="♀ (female)"]
  1K_3 = Resistor [tolerance=±5% resistance=1k power=0.25 package="1206 [SMD]"]
  2K_3 = Resistor [tolerance=±5% resistance=2.2 power=0.25 package="1206 [SMD]"]
  IND = female pin header, 2 pins [form="♀ (female)"]
  -_5V_+ = screw terminal, 2 pins
  J1 = screw terminal, 2 pins
  ELECTRODE = female pin header, 2 pins [form="♀ (female)"]
  +_5V_- = screw terminal, 2 pins

nets:
  N1: U1.VP, 10K.Pin_0, GSR.pin1
  N2: U1.VN, 1K_3.Pin_0, 2K_3.Pin_0
  N3: U1.D34, 1K_2.Pin_0, 2K.Pin_0
  N4: U1.D32, 1K.Pin_0, 2K_2.Pin_0
  N5: U1.D26, H-BRIDGE.pin6
  N6: U1.D27, H-BRIDGE.pin5
  N7: U1.D14, IND.pin2
  N8: U1.D12, H-BRIDGE.pin2
  N9: U1.D13, H-BRIDGE.pin1
  N10: U1.GND, H-BRIDGE.pin4, 2K.Pin_1, 10K.Pin_1, 2K_2.Pin_1, ECG(39).pin2, EOG(34).pin2, EEG(32).pin2, 2K_3.Pin_1
  N11: U1.Vin, GSR.pin2, ECG(39).pin1, EOG(34).pin1, EEG(32).pin1
  N12: U1.D21, OLED1.SDA
  N13: U1.D22, OLED1.SCK
  N14: OLED1.GND, IND.pin1, -_5V_+.pin1, +_5V_-.pin1
  N15: OLED1.VDD, H-BRIDGE.pin3, ON_---_OFF.P
  N16: ON_---_OFF.O, -_5V_+.pin2, +_5V_-.pin2
  N17: 1K.Pin_1, EEG(32).pin3
  N18: 1K_2.Pin_1, EOG(34).pin3
  N19: ECG(39).pin3, 1K_3.Pin_1
  N20: J1.pin1, ELECTRODE.pin1
  N21: J1.pin2, ELECTRODE.pin2

notes:
  HACKING
  HEURISTICS
  SENSOR BOARD

custom parts:
  LuaNode32 / ESP32: New Image for LuaNode32 DOIT ESP32 DEVKIT V1. Base parts from LuaNode32 / ESP32 ESP32 based LuaNode32 by G.Noorlander DOIT Esp32 DevKit v1 (30 pins long, 11 pins width) by Werner Rothschopf (modified by vanepp Dec 2018)
  OLED 128x64 I2C Monochrome Display GND-VDD: OLED 128x64 I2C Monochrome Display. Note: there are two variants of this part, this one is the GND VDD SCK SDA variant. The other is VDD GND SCK SDA. Make sure you select the part that matches your module as using the incorrect part will probably destroy your module! In addition the mounting holes are marked on silkscreen but not by default drilled. If you want drilled mounting holes, copy a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
